# Fritzing sketch arduinoCoffeeMachine (saved by Fritzing 1.0.1rc)
breadboards: 1

parts:
  LED1 = LED - 5mm [color="Red (633nm)" current=0.030 package="5 mm [THT]"]
  LED2 = LED - 5mm [color="Green (555nm)" current=0.030 package="5 mm [THT]"]
  R1 = Resistor [tolerance=±5% power=0.25 resistance=110 package=THT]
  R2 = Resistor [tolerance=±5% power=0.25 resistance=110 package=THT]
  U1 = LCD-16X2 [package=lcd-16x2_noholes]
  S1 = Pushbutton [package="[SMD]"]
  DHT1 = DHT11 Humitidy and Temperature Sensor (3 pins)
  HC-SR04_Sensor_1 = HC-SR04 Ultrasonic Distance Sensor
  Part2 = Thumb Joystick
  Part1 = Arduino Uno (Rev3)
  R3 = Trimmer Potentiometer [maximum_resistance=10kΩ knob_status=50% package=THT]
  R4 = Resistor [tolerance=±5% power=0.25 resistance=110 package=THT]
  R5 = Resistor [tolerance=±5% power=0.25 resistance=110 package=THT]

nets:
  GND: LED1.cathode, LED2.cathode, U1.VSS, U1.R_W, U1.K, DHT1.Gnd, HC-SR04_Sensor_1.GND, Part2.GND, Part1.GND, R3.leg1, R4.Pin_0
  N1: LED1.anode, R2.Pin_0
  N2: LED2.anode, R1.Pin_0
  N3: R1.Pin_1, Part1.D3_PWM
  N4: R2.Pin_1, Part1.A2
  VCC: U1.VDD, S1.Pin_1, S1.Pin_2, DHT1.Plus, HC-SR04_Sensor_1.VCC, Part2.VCC, Part1.5V, R3.leg2, R5.Pin_1
  N5: U1.VO, R3.wiper
  N6: U1.RS, Part1.D12/MISO
  N7: U1.E, Part1.D11_PWM/MOSI
  N8: U1.DB4, Part1.D5_PWM
  N9: U1.DB5, Part1.D4
  N10: U1.DB6, Part1.D13/SCK
  N11: U1.DB7, Part1.D2
  N12: U1.A, R5.Pin_0
  N13: S1.Pin_3, S1.Pin_4, Part1.D6_PWM, R4.Pin_1
  N14: DHT1.Signal, Part1.D7
  N15: HC-SR04_Sensor_1.TRIG, Part1.D8
  N16: HC-SR04_Sensor_1.ECHO, Part1.D9_PWM
  N17: Part2.SEL, Part1.D10_PWM/SS
  N18: Part2.HORZ, Part1.A0
  N19: Part2.VERT, Part1.A1

custom parts:
  DHT11 Humitidy and Temperature Sensor (3 pins): DHT11 Humidity and Temperature Sensor (3 pins).
